# Fritzing sketch vu meter (saved by Fritzing 0.9.3b)
stripboards: 1

parts:
  D2 = LED_BARGRAPH_10 [package=led_bargaph_10]  # not connected
  R4 = Resistor [tolerance=±5% resistance=1k package="2512 [SMD]"]
  R5 = Resistor [tolerance=±5% resistance=100k package="2512 [SMD]"]
  R6 = Resistor [tolerance=±5% resistance=220 package="2512 [SMD]"]  # not connected
  C4 = Electrolytic Capacitor [capacitance=1µF package="100 mil [THT, electrolytic]"]  # not connected
  C5 = Ceramic Capacitor [capacitance="100 nF" package="0603 [SMD, multilayer]"]  # not connected
  C6 = Ceramic Capacitor [capacitance="100 nF" package="0603 [SMD, multilayer]"]
  VCC2 = Battery
  R7 = Resistor [tolerance=±5% resistance=100k package="2512 [SMD]"]
  R8 = Resistor [tolerance=±5% resistance=1k package="2512 [SMD]"]
  IC1 = IC, DIP package, 14 pins [chip_label=IC]
  IC2 = IC, DIP package, 18 pins [chip_label=IC]

nets:
  N1: R4.Pin_0, VCC2.+
  N2: R4.Pin_1, C6.1, IC1.pin2, IC1.pin13
  N3: R5.Pin_0, C6.0, IC1.pin5, IC1.pin10
  N4: R5.Pin_1, VCC2.-, R8.Pin_1
  N5: R7.Pin_0, IC1.pin1, IC1.pin14, IC2.pin5, IC2.pin14
  N6: R7.Pin_1, R8.Pin_0
  N7: IC1.pin3, IC1.pin12
  N8: IC1.pin4, IC1.pin11
  N9: IC1.pin6, IC1.pin9
  N10: IC1.pin7, IC1.pin8
  N11: IC2.pin1, IC2.pin18
  N12: IC2.pin2, IC2.pin17
  N13: IC2.pin3, IC2.pin16
  N14: IC2.pin4, IC2.pin15
  N15: IC2.pin6, IC2.pin13
  N16: IC2.pin7, IC2.pin12
  N17: IC2.pin8, IC2.pin11
  N18: IC2.pin9, IC2.pin10
